# Fritzing sketch cookieClicker (saved by Fritzing 0.9.2b)
breadboards: 1

parts:
  Součástka1 = Arduino Uno (Rev3)
  LCD1 = LCD screen
  R1 = Rotary Potentiometer (Small) [maximum_resistance=100kΩ package=THT]
  R2 = Resistor [tolerance=±5% resistance=220 package=THT]
  S1 = Pushbutton [package="[THT]"]
  R3 = Resistor [tolerance=±5% resistance=220 package=THT]
  S2 = Pushbutton [package="[THT]"]
  R4 = Resistor [tolerance=±5% resistance=220 package=THT]

nets:
  N1: Součástka1.D11_PWM/MOSI, LCD1.E
  N2: Součástka1.D12/MISO, LCD1.RS
  N3: Součástka1.D2, LCD1.DB7
  N4: Součástka1.D3_PWM, LCD1.DB6
  N5: Součástka1.D4, LCD1.DB5
  N6: Součástka1.D5_PWM, LCD1.DB4
  N7: Součástka1.D6_PWM, S1.Pin_1, S1.Pin_2, R3.Pin_0
  N8: Součástka1.D7, S2.Pin_1, S2.Pin_2, R4.Pin_0
  5V: Součástka1.5V, LCD1.VDD, R1.leg1, R2.Pin_1, S1.Pin_3, S1.Pin_4, S2.Pin_3, S2.Pin_4
  GND: Součástka1.GND, LCD1.VSS, LCD1.R/W, LCD1.LED-, R1.leg2, R3.Pin_1, R4.Pin_1
  N9: LCD1.V0, R1.wiper
  N10: LCD1.LED+, R2.Pin_0
